# Fritzing sketch arduino-nano-33-ble-wifi-circuit-diagram (saved by Fritzing 0.9.4)
breadboards: 1

parts:
  Part1 = Arduino Nano 33 BLE Sense
  M1 = ESP-01 Breakout Board Breadboard Adapter [part_number=ESP8266]

nets:
  N1: Part1.TX, M1.RXD
  N2: Part1.RX, M1.TXD
  GND: Part1.GND, Part1.A7, M1.GND
  N3: Part1.D11/MOSI, Part1.+5V
  3V3: Part1.3V3, M1.CHPD, M1.VCC

custom parts:
  Arduino Nano 33 BLE Sense: The Nano 33 BLE Sense (without headers) is Arduino’s 3.3V AI enabled board in the smallest available form factor: 45x18mm! The Arduino Nano 33 BLE Sense is a completely new board on a well-known form factor. It comes with a series of embedded sensors: 9 axis inertial sensor: what makes this board ideal for wearable devices humidity, and temperature sensor: to get highly accurate measurements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
  ESP-01 Breakout Board Breadboard Adapter: Generic WiFi Module based on the ESP8266 with onboard PCB antenna and UART communications with breadboard friendly breakout board attached.
